# Fritzing sketch CircuitSketch (saved by Fritzing 0.9.2b)
breadboards: 1

parts:
  Part1 = Arduino Uno (Rev3)
  Part2 = Logic Level Converter
  U3 = EM406 GPS Connector [package=em406]
  Part3 = Electric Imp Breakout

nets:
  GND: Part1.GND, Part2.GND, U3.GND1, Part3.9
  N1: Part1.D2, U3.TX
  N2: Part1.D3_PWM, Part2.TX_HV
  3V3: Part1.3V3, Part2.LV, U3.VCC, Part3.8
  N3: Part1.5V, Part2.HV
  N4: Part2.TX_LV, Part3.4

custom parts:
  Electric Imp Breakout: Electric Imp Breakout Board with onboard 3.3V regulated power supply
